# Fritzing sketch smart-collect-iot (saved by Fritzing 0.9.3b)

parts:
  hc-sr1 = hc-sr04
  Componente1 = LCD1602-I2C
  M1 = AJ-SR04M Module [part_number=AJ-SR04M]
  M2 = AJ-SR04M Module [part_number=AJ-SR04M]
  CPU1 = NodeMCU WROOM ESP 32

nets:
  VCC: hc-sr1.VCC, Componente1.VCC, M1.VCC, M2.VCC, CPU1.pin_17
  N1: hc-sr1.Trig, CPU1.pin_19
  N2: hc-sr1.Echo, CPU1.pin_21
  GND: hc-sr1.GND, Componente1.GND, M1.GND, M2.GND, CPU1.pin_18
  N3: Componente1.SDA, CPU1.pin_27
  N4: Componente1.SCL, CPU1.pin_30
  N5: M1.Echo, CPU1.pin_23
  N6: M1.Trig, CPU1.pin_22
  N7: M2.Echo, CPU1.pin_24
  N8: M2.Trig, CPU1.pin_25

custom parts:
  LCD1602-I2C: A standard character display, usually with 2x16 characters. Comes in many colors with LCM1602 IIC attached.
  AJ-SR04M Module: AJ-SR04M Ultrasonic Distance Measuring Sensor Controller Module, 3-5V DC.
  NodeMCU WROOM ESP 32: 30 pol Development Kit
